# Fritzing sketch rain-psp (saved by Fritzing 0.9.6b)

parts:
  MCU1 = Raspberry Pi Zero
  J1 = shrouded pin header, 16 pins [form="♂ (shrouded male)"]

nets:
  N1: MCU1.pin_16, J1.pin8
  N2: MCU1.pin_19, J1.pin9
  N3: MCU1.pin_21, J1.pin10
  N4: MCU1.pin_22, J1.pin7
  N5: MCU1.pin_23, J1.pin11
  N6: MCU1.pin_24, J1.pin6
  N7: MCU1.pin_26, J1.pin5
  N8: MCU1.pin_27, J1.pin4
  N9: MCU1.pin_28, J1.pin12
  N10: MCU1.pin_31, J1.pin14
  N11: MCU1.pin_32, J1.pin3
  N12: MCU1.pin_33, J1.pin15
  N13: MCU1.pin_35, J1.pin16
  N14: MCU1.pin_36, J1.pin2
  N15: MCU1.pin_38, J1.pin1
